# Fritzing sketch bom_loa (saved by Fritzing 0.9.3b)
breadboards: 1

parts:
  R1 = Resistor [tolerance=±5% resistance=470 package=THT]
  R2 = Resistor [tolerance=±5% resistance=10k package=THT]
  U1 = Sharp PC817 [package=THT]
  Q1 = Basic FET P-Channel [package="TO220 [THT]"]
  D1 = Rectifier Diode [part_number=1N4001 package="300 mil [THT]"]
  M1 = DC Motor
  R3 = Resistor [tolerance=±5% resistance=470 package=THT]
  U2 = Sharp PC817 [package=THT]
  R4 = Resistor [tolerance=±5% resistance=10k package=THT]
  Q2 = NPN-Transistor [package="TO92 [THT]"]
  J1 = Piezo Speaker
  Part1 = Arduino Uno (Rev3)
  Power_plug1 = Power plug

nets:
  N1: R1.Pin_0, Part1.D4
  N2: R1.Pin_1, U1.Pin_1
  N3: R2.Pin_0, U1.Pin_3, Q1.gate
  N4: R2.Pin_1, Q1.source, D1.cathode, Q2.C, Power_plug1.VCC
  N5: U1.Pin_2, U2.Pin_2, Part1.GND
  N6: U1.Pin_4, M1.pin_2, U2.Pin_4, J1.pin2, Power_plug1.GND
  N7: Q1.drain, D1.anode, M1.pin_1
  N8: R3.Pin_0, Part1.D3_PWM
  N9: R3.Pin_1, U2.Pin_1
  N10: U2.Pin_3, R4.Pin_0
  N11: R4.Pin_1, Q2.E
  N12: Q2.B, J1.pin1

notes:
  12V
  Bơm
  Còi Buzzer
  IRF540
  C1815
