# Fritzing sketch mlx90614 (saved by Fritzing 0.9.3b)
breadboards: 1

parts:
  Part1 = Arduino Uno (Rev3)
  Mod1 = gy-906
  M1 = fc-51 [package=THT]

nets:
  N1: Part1.A1, M1.pin1
  N2: Part1.A4/SDA, Mod1.SDA
  N3: Part1.A5/SCL, Mod1.SCL
  3V3: Part1.3V3, Mod1.VIN, M1.pin3
  GND: Part1.GND, Mod1.GND, M1.pin2

custom parts:
  gy-906: gy-906 Non-contact PIR I2C interface temperature sensor breakout board.
