# Fritzing sketch nut nhan (saved by Fritzing 0.9.3b)
breadboards: 1

parts:
  Part1 = Arduino Uno (Rev3)
  R1 = Resistor [tolerance=±5% resistance=10k package=THT]
  C1 = Ceramic Capacitor [capacitance=100nF package="100 mil [THT, multilayer]"]
  S1 = Momentary Switch 6mm 2pin
  RE1 = Rotary Encoder [package=THT]

nets:
  N1: Part1.A3, RE1.EncoderPinC
  N2: Part1.GND, C1.1, S1.2, RE1.EncoderPinA
  N3: Part1.D2, R1.Pin_0
  N4: Part1.5V, RE1.EncoderPinB
  N5: R1.Pin_1, C1.0, S1.1

custom parts:
  Momentary Switch 6mm 2pin: Momentary Switch 6mm 2 pin Button commonly used for reset or general input.
